# Fritzing sketch basestation_rpi3 (saved by Fritzing 0.9.3b)
breadboards: 3

parts:
  Raspberry_Pi_1 = Raspberry Pi 3 [part_number=RPI-3-V1.2]
  OLED_I2C1 = OLED 128x64 I2C Monochrome Display
  Part2 = Adafruit TCA9548A
  OLED_I2C2 = OLED 128x64 I2C Monochrome Display
  OLED_I2C3 = OLED 128x64 I2C Monochrome Display
  OLED_I2C4 = OLED 128x64 I2C Monochrome Display
  S1 = Round Pushbutton
  R1 = Resistor [tolerance=±5% resistance=1k package="0805 [SMD]"]
  R2 = Resistor [tolerance=±5% resistance=1k package="0805 [SMD]"]
  S2 = Round Pushbutton
  S3 = Round Pushbutton
  S4 = Round Pushbutton
  S5 = Round Pushbutton
  S6 = Round Pushbutton
  S7 = Round Pushbutton
  S8 = Round Pushbutton
  S9 = Round Pushbutton

nets:
  VDD: Raspberry_Pi_1.3v3, Raspberry_Pi_1.3V3, OLED_I2C1.VDD, Part2.VCC, OLED_I2C2.VDD, OLED_I2C3.VDD, OLED_I2C4.VDD, R1.Pin_1, R2.Pin_0
  N1: Raspberry_Pi_1.GPIO2, Part2.INPUTSDA
  N2: Raspberry_Pi_1.GPIO3, Part2.INPUTSCL
  GND: Raspberry_Pi_1.GND, OLED_I2C1.GND, Part2.GND, OLED_I2C2.GND, OLED_I2C3.GND, OLED_I2C4.GND
  N3: Raspberry_Pi_1.GIPO10, S1.leg0
  N4: Raspberry_Pi_1.GIPO11, Part2.A0
  N5: Raspberry_Pi_1.GIPO6, S2.leg1
  N6: Raspberry_Pi_1.GIPO13, S3.leg1
  N7: Raspberry_Pi_1.GIPO19, S4.leg1
  N8: Raspberry_Pi_1.GIPO26, S5.leg1
  N9: Raspberry_Pi_1.GIPO21, S8.leg1
  N10: Raspberry_Pi_1.GIPO20, S7.leg1
  N11: Raspberry_Pi_1.GIPO16, S6.leg1
  N12: Raspberry_Pi_1.GIPO12, S9.leg1
  N13: Raspberry_Pi_1.GIPO7, Part2.A2
  N14: Raspberry_Pi_1.GIPO8, Part2.A1
  N15: OLED_I2C1.SDA, Part2.0SDA
  N16: OLED_I2C1.SCK, Part2.0SCL
  N17: Part2.2SDA, OLED_I2C3.SDA
  N18: Part2.2SCL, OLED_I2C3.SCK
  N19: Part2.3SDA, OLED_I2C4.SDA
  N20: Part2.3SCL, OLED_I2C4.SCK
  N21: Part2.1SDA, OLED_I2C2.SDA
  N22: Part2.1SCL, OLED_I2C2.SCK
  N23: S1.leg1, R1.Pin_0
  N24: R2.Pin_1, S6.leg0, S9.leg0

custom parts:
  Adafruit TCA9548A: You just found the perfect I2C sensor, and you want to wire up two or three or more of them to your Arduino when you realize "Uh oh, this chip has a fixed I2C address, and from what I know about I2C, you cannot have two devices with the same address on the same SDA/SCL pins!" Are you out of luck? You would be, if you didn't have this ultra-cool TCA9548A 1-to-8 I2C multiplexer! Finally, a way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
