# Fritzing sketch beltpack_rpi3 (saved by Fritzing 0.9.3b)
breadboards: 1

parts:
  Raspberry_Pi_1 = Raspberry Pi 3 [part_number=RPI-3-V1.2]
  Part1 = ADS1115  # not connected
  S1 = Round Pushbutton
  S2 = Toggle Switch [package=THT]
  R1 = Resistor [tolerance=±5% resistance=1k package="1206 [SMD]"]
  R2 = Resistor [tolerance=±5% resistance=1k package="1206 [SMD]"]
  R3 = Resistor [tolerance=±5% resistance=1k package="1206 [SMD]"]
  U1 = POT [package=pot_alpha_rv16af-20]
  OLED_I2C1 = OLED 128x64 I2C Monochrome Display

nets:
  3V3: Raspberry_Pi_1.3v3, R1.Pin_0, OLED_I2C1.VDD
  N1: Raspberry_Pi_1.GPIO2, OLED_I2C1.SDA
  N2: Raspberry_Pi_1.GPIO3, OLED_I2C1.SCK
  N3: Raspberry_Pi_1.GIPO4, U1.E, OLED_I2C1.GND
  N4: Raspberry_Pi_1.GIPO19, S1.leg0
  N5: Raspberry_Pi_1.GIPO26, R3.Pin_1
  N6: Raspberry_Pi_1.GIPO21, S2.L2
  N7: Raspberry_Pi_1.GIPO20, R2.Pin_1
  N8: Raspberry_Pi_1.GIPO16, S2.L1
  N9: S1.leg1, R3.Pin_0
  N10: S2.COM, R2.Pin_0
  N11: R1.Pin_1, U1.A

notes:
  Power off button
  2-way press to talk
  Volume control

custom parts:
  ADS1115: ADC ADS1115
